# Fritzing sketch 00.led (saved by Fritzing 0.9.3b)
breadboards: 1

parts:
  Composant3 = Adafruit HUZZAH32 ESP32 Feather [part_number="Adafruit #3405"]
  LED2 = LED - 5mm [color="Red (633nm)" package="5 mm [THT]"]
  R4 = Resistor [tolerance=±5% resistance=220 package=THT]

nets:
  N1: Composant3.GND, R4.Pin_0
  N2: Composant3.IO12_A11, LED2.anode
  N3: LED2.cathode, R4.Pin_1
