# Fritzing sketch 01.button (saved by Fritzing 0.9.3b)
breadboards: 1

parts:
  S1 = Pushbutton [package="[THT]"]
  R1 = Resistor [tolerance=±5% resistance=10k package=THT]
  LED1 = LED - 5mm [color="Red (633nm)" package="5 mm [THT]"]
  R2 = Resistor [tolerance=±5% resistance=220 package=THT]
  Composant2 = Adafruit HUZZAH32 ESP32 Feather [part_number="Adafruit #3405"]

nets:
  N1: S1.Pin_1, S1.Pin_2, Composant2.3.3V
  N2: S1.Pin_3, S1.Pin_4, R1.Pin_1, Composant2.IO14_A6
  N3: R1.Pin_0, R2.Pin_0, Composant2.GND
  N4: LED1.cathode, R2.Pin_1
  N5: LED1.anode, Composant2.IO12_A11
