# Fritzing sketch 03.potentiometer (saved by Fritzing 0.9.3b)
breadboards: 1

parts:
  U2 = POT [package=pot_mammoth]
  Composant2 = Adafruit HUZZAH32 ESP32 Feather [part_number="Adafruit #3405"]

nets:
  N1: U2.S, Composant2.GND
  N2: U2.A, Composant2.A0_DAC2
  N3: U2.E, Composant2.3.3V
