# Fritzing sketch 04.multi-led+potentiometer (saved by Fritzing 0.9.3b)
circuit board: 6.88566cm x 5.36311cm
breadboards: 1

parts:
  LED2 = LED - 5mm [color="Red (633nm)" package="5 mm [THT]"]
  LED3 = LED - 5mm [color="Green (555nm)" package="5 mm [THT]"]
  LED6 = LED - 5mm [color="Yellow (595nm)" package="5 mm [THT]"]
  R9 = Resistor [tolerance=±5% resistance=220 package=THT]
  R10 = Resistor [tolerance=±5% resistance=220 package=THT]
  R11 = Resistor [tolerance=±5% resistance=220 package=THT]
  Composant1 = Adafruit HUZZAH32 ESP32 Feather [part_number="Adafruit #3405"]
  R12 = Resistor [tolerance=±5% resistance=220 package=THT]
  S1 = Pushbutton [package="[THT]"]

nets:
  N1: LED2.cathode, LED3.cathode, LED6.cathode, Composant1.GND, R12.Pin_0
  N2: LED2.anode, R9.Pin_1
  N3: LED3.anode, R10.Pin_1
  N4: LED6.anode, R11.Pin_1
  N5: R9.Pin_0, Composant1.IO12_A11
  N6: R10.Pin_0, Composant1.IO27_A10
  N7: R11.Pin_0, Composant1.IO33_A9
  N8: Composant1.3.3V, S1.Pin_1, S1.Pin_2
  N9: Composant1.IO14_A6, R12.Pin_1, S1.Pin_3, S1.Pin_4

notes:
  CHASER_LIGHTS

// code stored in the sketch: ChaserLights.ino
/*
  chaserlights
  
  This example is part of the Fritzing Creator Kit: www.fritzing.org/creator-kit.
*/

int pinsCount=8;                        // declaring the integer variable pinsCount
int pins[] = {2,3,4,5,6,7,8,9};          // declaring the array pins[]

void setup() {                
  for (int i=0; i<pinsCount; i=i+1){    // counting the variable i from 0 to 7
    pinMode(pins[i], OUTPUT);            // initialising the pin at index i of the array of pins as OUTPUT
  }
}

void loop() {
  for (int i=0; i<pinsCount; i=i+1){    // chasing right
    digitalWrite(pins[i], HIGH);         // switching the LED at index i on
    delay(100);                          // stopping the program for 100 milliseconds
    digitalWrite(pins[i], LOW);          // switching the LED at index i off
  }
  for (int i=pinsCount-1; i>0; i=i-1){   // chasing left (except the outer leds)
    digitalWrite(pins[i], HIGH);         // switching the LED at index i on
    delay(100);                          // stopping the program for 100 milliseconds
    digitalWrite(pins[i], LOW);          // switching the LED at index i off
  }
}
