# Fritzing sketch 05.phototransistor (saved by Fritzing 0.9.3b)
breadboards: 1

parts:
  R1 = Resistor [tolerance=±5% resistance=10k package=THT]
  Composant2 = Adafruit HUZZAH32 ESP32 Feather [part_number="Adafruit #3405"]
  Q1 = LTR-301 [package=ltr-301]

nets:
  N1: R1.Pin_0, Composant2.A0_DAC2, Q1.C
  N2: R1.Pin_1, Composant2.GND
  N3: Composant2.3.3V, Q1.E
