# Fritzing sketch bme680 (saved by Fritzing 0.9.3b)

parts:
  Composant3 = Adafruit HUZZAH32 ESP32 Feather [part_number="Adafruit #3405"]
  Composant4 = Adafruit_BMP280

nets:
  GND: Composant3.GND, Composant4.GND
  3.3V: Composant3.3.3V, Composant4.VIN
  N1: Composant3.SCL, Composant4.SCK/SCL
  N2: Composant3.SDA, Composant4.SDI/SDA

custom parts:
  Adafruit_BMP280: Bosch has stepped up their game with their new BMP280 sensor, an environmental sensor with temperature, barometric pressure that is the next generation upgrade to the BMP085/BMP180/BMP183. This sensor is great for all sorts of weather sensing and can even be used in both I2C and SPI! This precision sensor from Bosch is the best low-cost, precision sensing solution for measuring barometric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
