# Fritzing sketch projet (saved by Fritzing 0.9.3b)
breadboards: 1

parts:
  Composant1 = Adafruit HUZZAH32 ESP32 Feather [part_number="Adafruit #3405"]
  Composant2 = Adafruit_BMP280
  Q1 = LTR-301 [package=ltr-301]
  S1 = Round Pushbutton  # not connected
  S2 = Round Pushbutton  # not connected
  LED1 = LED - 5mm [color="Green (565nm)" package="5 mm [THT]"]
  LED2 = LED - 5mm [color="Red (633nm)" package="5 mm [THT]"]
  R1 = Resistor [tolerance=±5% resistance=330 package=THT]
  R2 = Resistor [tolerance=±5% resistance=330 package=THT]
  R3 = Resistor [tolerance=±5% resistance=10k package=THT]

nets:
  N1: Composant1.SCK, Q1.E, R3.Pin_0
  N2: Composant1.IO12_A11, LED2.anode
  N3: Composant1.IO27_A10, LED1.anode
  N4: Composant1.SCL, Composant2.SCK/SCL
  N5: Composant1.SDA, Composant2.SDI/SDA
  N6: Q1.C, R1.Pin_0, R2.Pin_0
  N7: LED1.cathode, R1.Pin_1
  N8: LED2.cathode, R2.Pin_1

custom parts:
  Adafruit_BMP280: Bosch has stepped up their game with their new BMP280 sensor, an environmental sensor with temperature, barometric pressure that is the next generation upgrade to the BMP085/BMP180/BMP183. This sensor is great for all sorts of weather sensing and can even be used in both I2C and SPI! This precision sensor from Bosch is the best low-cost, precision sensing solution for measuring barometric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
